# Fritzing sketch esp01-devboard (saved by Fritzing 0.9.3b)
circuit board: 6.87304cm x 5.1272cm
breadboards: 1

parts:
  J1 = female pin header, 4 pins [form="♀ (female)"]
  J2 = female pin header, 4 pins [form="♀ (female)"]
  J3 = female pin header, 4 pins [form="♀ (female)"]
  J4 = female pin header, 4 pins [form="♀ (female)"]
  J5 = female pin header, 4 pins [form="♀ (female)"]
  J6 = female pin header, 5 pins [form="♀ (female)"]
  J7 = Dagu DGServo 9g header (male) [package=THT]
  U1 = Voltage Regulator - Variable [package="TO220 [THT]"]
  R1 = Resistor [tolerance=±5% resistance=56k package=THT]
  R2 = Resistor [tolerance=±5% resistance=10k package=THT]
  R3 = Resistor [tolerance=±5% resistance=10k package=THT]
  R4 = Resistor [tolerance=±5% resistance=3.3k package=THT]
  S1 = Pushbutton [package=THT]
  VCC1 = Battery block 9V
  C1 = Electrolytic Capacitor [capacitance=10µF package="100 mil [THT, electrolytic]"]

nets:
  N1: J1.pin1, J1.pin2, J1.pin3, J1.pin4, J4.pin4, U1.OUT, R2.Pin_0, R3.Pin_0, R4.Pin_1, C1.+
  N2: J2.pin1, J2.pin2, J2.pin3, J2.pin4, J5.pin1, J6.pin1, J7.gnd, R1.Pin_1, S1.leg1, VCC1.-, C1.-
  N3: J3.pin1, J5.pin3, J7.Vcc
  N4: J3.pin4, J5.pin2
  N5: J4.pin1, J6.pin2
  N6: J4.pin2, R3.Pin_1
  N7: J4.pin3, R2.Pin_1, S1.leg0
  N8: J5.pin4, J6.pin3
  N9: U1.ADJ, R1.Pin_0, R4.Pin_0
  N10: U1.IN, VCC1.+
